// Logisim project Carry_Select_Adder.circ as structural Verilog: 1 circuit, main circuit main
module main (
  input  [5:0] A,
  input  [5:0] B,
  input  Cin,
  output [5:0] S,
  output Cout
);

  wire adder_1_cout, adder_2_cout, adder_4_cout, adder_5_cout, C1, C2;
  wire [1:0] adder_1_out, adder_2_out, adder_4_out, adder_5_out;

  Adder #(.width(2)) adder_1 (.a(A[5:4]), .b(B[5:4]), .out(adder_1_out), .cin(1'b0), .cout(adder_1_cout));
  Adder #(.width(2)) adder_2 (.a(A[5:4]), .b(B[5:4]), .out(adder_2_out), .cin(1'b1), .cout(adder_2_cout));
  Adder #(.width(2)) adder_3 (.a(A[1:0]), .b(B[1:0]), .out(S[1:0]), .cin(Cin), .cout(C1));
  Adder #(.width(2)) adder_4 (.a(A[3:2]), .b(B[3:2]), .out(adder_4_out), .cin(1'b0), .cout(adder_4_cout));
  Adder #(.width(2)) adder_5 (.a(A[3:2]), .b(B[3:2]), .out(adder_5_out), .cin(1'b1), .cout(adder_5_cout));
  Multiplexer #(.width(2)) multiplexer_1 (.in0(adder_1_out), .in1(adder_2_out), .out(S[5:4]), .sel(C2));
  Multiplexer multiplexer_2 (.in0(adder_1_cout), .in1(adder_2_cout), .out(Cout), .sel(C2));
  Multiplexer #(.width(2)) multiplexer_3 (.in0(adder_4_out), .in1(adder_5_out), .out(S[3:2]), .sel(C1));
  Multiplexer multiplexer_4 (.in0(adder_4_cout), .in1(adder_5_cout), .out(C2), .sel(C1));

  // Other names for the same wires on the sheet: A10[1:0] = A[1:0]; A32[1:0] = A[3:2]; A54[1:0] = A[5:4];
  //   B10[1:0] = B[1:0]; B32[1:0] = B[3:2]; B54[1:0] = B[5:4]; S10[1:0] = S[1:0]; S32[1:0] = S[3:2];
  //   S54[1:0] = S[5:4]
endmodule
